// Logisim project hw5evolution.circ as structural Verilog: 11 circuits, main circuit MyXOR
module MyXOR (
  input  in_1,
  input  in_2,
  output out_3
);

  wire and_1_out, and_2_out, not_1_out, not_2_out;

  not not_1 (not_1_out, in_1);
  not not_2 (not_2_out, in_2);
  and and_1 (and_1_out, not_2_out, in_1);
  and and_2 (and_2_out, in_2, not_1_out);
  or or_1 (out_3, and_1_out, and_2_out);

  // Notes on the sheet:
  //   Here is a location to build an XOR circuit
  //   You can follow the tutorial (Help menu - "tutorial") or work on your own...
endmodule

module FullAdder (
  input  X,
  input  Y,
  input  CarryIn,
  output Sum,
  output CarryOut
);

  wire and_1_out, and_2_out, and_3_out, and_4_out, and_5_out, and_6_out, and_7_out, and_8_out, not_1_out,
       not_2_out, not_3_out;

  not not_1 (not_1_out, X);
  not not_2 (not_2_out, Y);
  not not_3 (not_3_out, CarryIn);
  and and_1 (and_1_out, not_1_out, not_2_out, CarryIn);
  and and_2 (and_2_out, not_1_out, Y, not_3_out);
  and and_3 (and_3_out, X, not_3_out, not_2_out);
  and and_4 (and_4_out, X, CarryIn, Y);
  and and_5 (and_5_out, CarryIn, Y, not_1_out);
  and and_6 (and_6_out, CarryIn, not_2_out, X);
  and and_7 (and_7_out, Y, X, not_3_out);
  and and_8 (and_8_out, CarryIn, X, Y);
  or or_1 (Sum, and_1_out, and_2_out, and_3_out, and_4_out);
  or or_2 (CarryOut, and_5_out, and_6_out, and_7_out, and_8_out);

  // Notes on the sheet:
  //   3 input bits:  X,  Y,  and CarryIn
  //   Here is a location to build an FULL ADDER circuit
  //   (1) draw the other four rails   (2) you'll need 8 AND gates    (3)  you'll need 2 OR gates
  //   two output bits:  Sum and CarryOut
endmodule

module A_4bit_Ripple_Carry_Adder (
  input  Y3,
  input  Y2,
  input  Y1,
  input  Y0,
  input  X3,
  input  X2,
  input  X1,
  input  X0,
  output Sum4,
  output Sum3,
  output Sum2,
  output Sum1,
  output Sum0
);

  wire fulladder_2_carryout, fulladder_3_carryout, fulladder_4_carryout;

  FullAdder fulladder_1 (.X(Y3), .Y(X3), .CarryIn(fulladder_2_carryout), .Sum(Sum3), .CarryOut(Sum4));
  FullAdder fulladder_2 (.X(Y2), .Y(X2), .CarryIn(fulladder_3_carryout), .Sum(Sum2), .CarryOut(fulladder_2_carryout));
  FullAdder fulladder_3 (.X(Y1), .Y(X1), .CarryIn(fulladder_4_carryout), .Sum(Sum1), .CarryOut(fulladder_3_carryout));
  FullAdder fulladder_4 (.X(Y0), .Y(X0), .CarryIn(1'b0), .Sum(Sum0), .CarryOut(fulladder_4_carryout));

  // Notes on the sheet:
  //   Here is a location to build an 4-bit RIPPLE-CARRY ADDER circuit
  //   8 input bits
  //   5 output bits
endmodule

module A_4bit_Multiplier (
  input  Y3,
  input  Y2,
  input  Y1,
  input  Y0,
  input  X3,
  input  X2,
  input  X1,
  input  X0,
  output Z7,
  output out_10,
  output out_11,
  output out_12,
  output out_13,
  output out_14,
  output out_15,
  output Z0
);

  wire a_4bit_ripple_carry_adder_2_sum1, a_4bit_ripple_carry_adder_2_sum2, a_4bit_ripple_carry_adder_2_sum3,
       a_4bit_ripple_carry_adder_2_sum4, a_4bit_ripple_carry_adder_3_sum1, a_4bit_ripple_carry_adder_3_sum2,
       a_4bit_ripple_carry_adder_3_sum3, a_4bit_ripple_carry_adder_3_sum4, a_4x1_multiplier_1_z0,
       a_4x1_multiplier_1_z1, a_4x1_multiplier_1_z2, a_4x1_multiplier_1_z3, a_4x1_multiplier_2_z0,
       a_4x1_multiplier_2_z1, a_4x1_multiplier_2_z2, a_4x1_multiplier_2_z3, a_4x1_multiplier_3_z0,
       a_4x1_multiplier_3_z1, a_4x1_multiplier_3_z2, a_4x1_multiplier_3_z3, a_4x1_multiplier_4_z1,
       a_4x1_multiplier_4_z2, a_4x1_multiplier_4_z3;

  A_4bit_Ripple_Carry_Adder a_4bit_ripple_carry_adder_1 (
    .Y3(a_4x1_multiplier_1_z3), .X3(a_4bit_ripple_carry_adder_2_sum4), .Y2(a_4x1_multiplier_1_z2),
    .X2(a_4bit_ripple_carry_adder_2_sum3), .Y1(a_4x1_multiplier_1_z1), .X1(a_4bit_ripple_carry_adder_2_sum2),
    .Y0(a_4x1_multiplier_1_z0), .X0(a_4bit_ripple_carry_adder_2_sum1), .Sum4(Z7), .Sum3(out_10),
    .Sum2(out_11), .Sum1(out_12), .Sum0(out_13));
  A_4x1_multiplier a_4x1_multiplier_1 (
    .y3(Y3), .y2(Y2), .y1(Y1), .y0(Y0), .x0(X3), .z0(a_4x1_multiplier_1_z0), .z1(a_4x1_multiplier_1_z1),
    .z2(a_4x1_multiplier_1_z2), .z3(a_4x1_multiplier_1_z3));
  A_4x1_multiplier a_4x1_multiplier_2 (
    .y3(Y3), .y2(Y2), .y1(Y1), .y0(Y0), .x0(X2), .z0(a_4x1_multiplier_2_z0), .z1(a_4x1_multiplier_2_z1),
    .z2(a_4x1_multiplier_2_z2), .z3(a_4x1_multiplier_2_z3));
  A_4bit_Ripple_Carry_Adder a_4bit_ripple_carry_adder_2 (
    .Y3(a_4x1_multiplier_2_z3), .X3(a_4bit_ripple_carry_adder_3_sum4), .Y2(a_4x1_multiplier_2_z2),
    .X2(a_4bit_ripple_carry_adder_3_sum3), .Y1(a_4x1_multiplier_2_z1), .X1(a_4bit_ripple_carry_adder_3_sum2),
    .Y0(a_4x1_multiplier_2_z0), .X0(a_4bit_ripple_carry_adder_3_sum1),
    .Sum4(a_4bit_ripple_carry_adder_2_sum4), .Sum3(a_4bit_ripple_carry_adder_2_sum3),
    .Sum2(a_4bit_ripple_carry_adder_2_sum2), .Sum1(a_4bit_ripple_carry_adder_2_sum1), .Sum0(out_14));
  A_4x1_multiplier a_4x1_multiplier_3 (
    .y3(Y3), .y2(Y2), .y1(Y1), .y0(Y0), .x0(X1), .z0(a_4x1_multiplier_3_z0), .z1(a_4x1_multiplier_3_z1),
    .z2(a_4x1_multiplier_3_z2), .z3(a_4x1_multiplier_3_z3));
  A_4bit_Ripple_Carry_Adder a_4bit_ripple_carry_adder_3 (
    .Y3(a_4x1_multiplier_3_z3), .X3(1'b0), .Y2(a_4x1_multiplier_3_z2), .X2(a_4x1_multiplier_4_z3),
    .Y1(a_4x1_multiplier_3_z1), .X1(a_4x1_multiplier_4_z2), .Y0(a_4x1_multiplier_3_z0),
    .X0(a_4x1_multiplier_4_z1), .Sum4(a_4bit_ripple_carry_adder_3_sum4),
    .Sum3(a_4bit_ripple_carry_adder_3_sum3), .Sum2(a_4bit_ripple_carry_adder_3_sum2),
    .Sum1(a_4bit_ripple_carry_adder_3_sum1), .Sum0(out_15));
  A_4x1_multiplier a_4x1_multiplier_4 (
    .y3(Y3), .y2(Y2), .y1(Y1), .y0(Y0), .x0(X0), .z0(Z0), .z1(a_4x1_multiplier_4_z1),
    .z2(a_4x1_multiplier_4_z2), .z3(a_4x1_multiplier_4_z3));

  // Notes on the sheet:
  //   factor (4 bits)
  //   See the problem for details on this hint:   Build a 4x1-bit multiplier first!
  //   second factor (4 bits)
  //   product (8 bits)
  //   4-bit MULTIPLIER circuit
  //   most significant (highest) output bit
  //   least significant (lowest) output bit
endmodule

module A_3by2_divider (
  input  Y2,
  input  Y1,
  input  Y0,
  input  X1,
  input  X0,
  output Z2,
  output Z1,
  output Z0,
  output Error
);

  wire and_2_out, and_3_out, not_1_out, not_2_out, not_3_out;

  not not_1 (not_1_out, X0);
  not not_2 (not_2_out, X0);
  not not_3 (not_3_out, X1);
  and and_1 (Z2, Y2, X0);
  and and_2 (and_2_out, not_1_out, Y2, Y1, X1);
  and and_3 (and_3_out, X0, Y1);
  and and_4 (Z0, X0, Y0);
  and and_5 (Error, not_2_out, not_3_out);
  or or_1 (Z1, and_2_out, and_3_out);

  // Notes on the sheet:
  //   Dividend (3 bits: Y2 Y1 Y0)
  //   Divisor (2 bits: X1 X0)
  //   Quotient (4 bits: Z2 Z1 Z0 and Error)
  //   3-by-2-bit DIVIDER circuit
endmodule

module A_2bit_decoder (
);


  // Notes on the sheet:
  //   2-bit DECODER circuit (extra credit - see hw)
endmodule

module A_12nGb_memory (
);


  // Notes on the sheet:
  //   12 nanogigabit MEMORY circuit (extra credit - see hw)
endmodule

module A_4x1_multiplier (
  input  y3,
  input  y2,
  input  y1,
  input  y0,
  input  x0,
  output z0,
  output z1,
  output z2,
  output z3
);

  and and_1 (z0, x0, y0);
  and and_2 (z1, x0, y1);
  and and_3 (z2, y2, x0);
  and and_4 (z3, y3, x0);
endmodule

module A_divideby1 (
  input  Y2,
  input  Y1,
  input  Y0,
  input  X1,
  input  X0,
  output Z2,
  output Z1,
  output Z0
);

  wire not_1_out, not_2_out, not_3_out;

  not not_1 (not_1_out, X1);
  not not_2 (not_2_out, X1);
  not not_3 (not_3_out, X1);
  and and_1 (Z2, Y2, not_1_out, X0);
  and and_2 (Z1, Y1, not_2_out, X0);
  and and_3 (Z0, Y0, not_3_out, X0);
endmodule

module A_divideby2 (
  input  Y2,
  input  Y1,
  input  Y0,
  input  X1,
  input  X0,
  output Z1,
  output Z0
);

  wire not_1_out, not_2_out;

  not not_1 (not_1_out, X0);
  not not_2 (not_2_out, X0);
  and and_1 (Z1, Y2, X1, not_1_out);
  and and_2 (Z0, Y1, X1, not_2_out);

  // Notes on the sheet:
  //   When you divide by 2, the least sig. bit will be removed so it does nothing here!
endmodule

module A_divideby3 (
  input  Y2,
  input  Y1,
  input  Y0,
  input  X1,
  input  X0,
  output Z1,
  output Z0
);

  wire and_1_out, and_2_out, and_3_out, not_1_out, not_2_out, not_3_out, not_4_out, or_1_out;

  not not_1 (not_1_out, Y1);
  not not_2 (not_2_out, Y2);
  not not_3 (not_3_out, Y1);
  not not_4 (not_4_out, Y0);
  and and_1 (and_1_out, not_4_out, Y2, not_1_out);
  and and_2 (and_2_out, Y0, not_2_out, Y1);
  and and_3 (and_3_out, Y0, not_3_out, Y2);
  or or_1 (or_1_out, and_1_out, and_2_out, and_3_out);
  and and_4 (Z1, Y2, X1, Y1, X0);
  and and_5 (Z0, X1, or_1_out, X0);
endmodule
